# Fritzing sketch frankenkorg (saved by Fritzing 0.9.3b)
breadboards: 1

parts:
  Atmega1 = ATmega644 [package=pdpi]
  J1 = AVR ISP 6 Pin [package=2x3_offset]
  R1 = Resistor [tolerance=±5% resistance=10k package=THT]
  IC1 = IC, DIP package, 16 pins [chip_label=74LS138]
  J3 = male pin header, 9 pins [form="♂ (male)"]
  IC2 = IC, DIP package, 16 pins [chip_label=74LS138]
  J2 = male pin header, 9 pins [form="♂ (male)"]
  IC3 = IC, DIP package, 16 pins [chip_label=74LS138]
  J4 = male pin header, 8 pins [form="♂ (male)"]
  J5 = male pin header, 10 pins [form="♂ (male)"]
  J6 = male pin header, 14 pins [form="♂ (male)"]
  R2 = Resistor [tolerance=±5% resistance=220 package=THT]
  J7 = male pin header, 5 pins [form="♂ (male)"]
  R3 = Resistor [tolerance=±5% resistance=220 package=THT]
  IC4 = Voltage Regulator [package=to220-igo]
  C1 = Electrolytic Capacitor [capacitance=10µF package="100 mil [THT, electrolytic]"]
  C2 = Electrolytic Capacitor [capacitance=10µF package="100 mil [THT, electrolytic]"]
  J8 = male pin header, 6 pins [form="♂ (male)"]

nets:
  N1: Atmega1.PB0, IC1.pin3
  N2: Atmega1.PB1, IC1.pin2
  N3: Atmega1.PB2, IC1.pin1
  N4: Atmega1.PB5, J1.4
  N5: Atmega1.PB6, J1.1
  N6: Atmega1.PB7, J1.3
  N7: Atmega1.RESET, J1.5, R1.Pin_1
  N8: Atmega1.VCC, Atmega1.AVCC, Atmega1.AREF, IC2.pin6, IC2.pin16, IC3.pin6, IC3.pin16, R3.Pin_1
  GND: Atmega1.GND, J1.6, IC1.pin4, IC1.pin5, IC1.pin8, J3.pin1, IC2.pin4, IC2.pin5, IC2.pin8, J2.pin9, IC3.pin4, IC3.pin5, IC3.pin8, J7.pin3, J7.pin5, IC4.GND, J8.pin2
  N9: Atmega1.PD1, R2.Pin_1
  N10: Atmega1.PD2, IC2.pin3
  N11: Atmega1.PD3, IC2.pin2
  N12: Atmega1.PD4, IC2.pin1
  N13: Atmega1.PD5, IC3.pin2
  N14: Atmega1.PD6, IC3.pin1
  N15: Atmega1.PD7, J4.pin7, J5.pin8, J6.pin8
  N16: Atmega1.PC0, J4.pin6, J5.pin7, J6.pin7
  N17: Atmega1.PC1, J4.pin5, J5.pin6, J6.pin6
  N18: Atmega1.PC2, J4.pin4, J5.pin5, J6.pin5
  N19: Atmega1.PC3, J4.pin3, J5.pin4, J6.pin4
  N20: Atmega1.PC4, J4.pin2, J5.pin3, J6.pin3
  N21: Atmega1.PC5, J4.pin1, J5.pin2, J6.pin2
  N22: Atmega1.PC6, J5.pin1, J6.pin1
  N23: Atmega1.PC7, IC3.pin3
  N24: Atmega1.PA3, J8.pin6
  N25: Atmega1.PA2, J8.pin5
  N26: Atmega1.PA1, J8.pin4
  N27: Atmega1.PA0, J8.pin3
  5V: J1.2, R1.Pin_0, IC1.pin6, IC1.pin16, IC4.OUT, C2.+, J8.pin1
  N28: IC1.pin7, J2.pin8
  N29: IC1.pin9, J2.pin7
  N30: IC1.pin10, J2.pin6
  N31: IC1.pin11, J2.pin5
  N32: IC1.pin12, J2.pin4
  N33: IC1.pin13, J2.pin3
  N34: IC1.pin14, J2.pin2
  N35: IC1.pin15, J2.pin1
  N36: J3.pin2, IC2.pin7
  N37: J3.pin3, IC2.pin9
  N38: J3.pin4, IC2.pin10
  N39: J3.pin5, IC2.pin11
  N40: J3.pin6, IC2.pin12
  N41: J3.pin7, IC2.pin13
  N42: J3.pin8, IC2.pin14
  N43: J3.pin9, IC2.pin15
  N44: IC3.pin7, J5.pin9
  N45: IC3.pin9, J4.pin8, J5.pin10
  N46: IC3.pin10, J6.pin9
  N47: IC3.pin11, J6.pin10
  N48: IC3.pin12, J6.pin11
  N49: IC3.pin13, J6.pin12
  N50: IC3.pin14, J6.pin13
  N51: IC3.pin15, J6.pin14
  N52: R2.Pin_0, J7.pin2
  N53: J7.pin1, R3.Pin_0
  N54: J7.pin4, IC4.IN, C1.+
  N55: C1.-, C2.-
